# Fritzing sketch schematic (saved by Fritzing 0.9.3b)
breadboards: 1

parts:
  Part1 = Arduino Uno (Rev3)
  R1 = Resistor [tolerance=±5% resistance=10k package=THT]
  S1 = Toggle Switch [package=THT]
  S2 = Toggle Switch [package=THT]
  S3 = Toggle Switch [package=THT]
  S4 = Toggle Switch [package=THT]
  R5 = Resistor [tolerance=±5% resistance=10k package=THT]
  R6 = Resistor [tolerance=±5% resistance=10k package=THT]
  R7 = Resistor [tolerance=±5% resistance=10k package=THT]

nets:
  N1: Part1.D2, R1.Pin_0, S1.COM
  N2: Part1.D3_PWM, S3.COM, R5.Pin_0
  N3: Part1.D4, S2.COM, R6.Pin_0
  N4: Part1.D5_PWM, S4.COM, R7.Pin_0
  N5: Part1.5V, R1.Pin_1, R5.Pin_1, R6.Pin_1, R7.Pin_1
  N6: Part1.GND, S1.L1, S2.L1, S3.L1, S4.L1
